# Fritzing sketch sens_umid_DIY (saved by Fritzing 0.9.3b)
breadboards: 1

parts:
  Part2 = Arduino Uno (Rev3) - ICSP
  Part3 = Soil Moisture Sensor
  R1 = Resistor [tolerance=±5% resistance=10k package=THT]
  DS1 = DS18B20 1-Wire Temperature Sensor [part_number=DS18B20]
  R2 = Resistor [tolerance=±5% resistance=4.7k package="2010 [SMD]"]
  R3 = Resistor [tolerance=±5% resistance=10k package=THT]
  DHT1 = DHT11 Humitidy and Temperature Sensor

nets:
  N1: Part2.A0, Part3.SIG, R1.Pin_0
  N2: Part2.A1, R3.Pin_0, DHT1.DATA
  N3: Part2.D2, DS1.DQ, R2.Pin_1
  VDD: Part2.5V, R1.Pin_1, DS1.VDD, R2.Pin_0, R3.Pin_1, DHT1.VDD
  GND: Part2.GND, Part3.GND, DS1.GND, DHT1.GND

custom parts:
  DHT11 Humitidy and Temperature Sensor: DHT11 Humidity and Temperature Sensor
